// Digital circuit Lab02.dig as structural Verilog
module Lab02 (
  input  B,
  input  C,
  input  A,
  input  D,
  output Fa,
  output Fb,
  output Fc,
  output Fd,
  output Fe,
  output Fg,
  output Ff
);

  wire not_A, not_B, not_C, not_D, Seg_A_1, Seg_A_2, Seg_A_3, Seg_A_4, Seg_A_5, Seg_B_1, Seg_B_2, Seg_B_3,
       Seg_B_4, Seg_B_5, Seg_C_1, Seg_C_2, Seg_C_3, Seg_C_4, Seg_C_5, Seg_D_1, Seg_D_2, Seg_D_3, Seg_D_4,
       Seg_D_5, Seg_D_6, Seg_E_1, Seg_E_2, Seg_E_3, Seg_E_4, Seg_F_1, Seg_F_2, Seg_F_3, Seg_F_4, Seg_F_5,
       Seg_G_1, Seg_G_2, Seg_G_3;

  not not_1 (not_A, A);
  not not_2 (not_B, B);
  not not_3 (not_C, C);
  not not_4 (not_D, D);
  and and_1 (Seg_A_1, not_B, not_D);
  and and_2 (Seg_A_2, C, B);
  and and_3 (Seg_A_3, not_A, C);
  and and_4 (Seg_A_4, B, not_A, D);
  and and_5 (Seg_A_5, not_B, A, not_C);
  and and_6 (Seg_B_1, not_A, C, D);
  and and_7 (Seg_B_2, not_C, not_B);
  and and_8 (Seg_B_3, not_B, not_D);
  and and_9 (Seg_B_4, A, not_C, D);
  and and_10 (Seg_B_5, not_A, not_C, not_D);
  and and_11 (Seg_C_1, A, not_B);
  and and_12 (Seg_C_2, not_C, D);
  and and_13 (Seg_C_3, not_A, B);
  and and_14 (Seg_C_4, not_A, D);
  and and_15 (Seg_C_5, not_B, not_C);
  and and_16 (Seg_D_1, A, B, not_D);
  and and_17 (Seg_D_2, not_C, not_B, not_D);
  and and_18 (Seg_D_3, B, not_C, D);
  and and_19 (Seg_D_4, not_A, C, not_D);
  and and_20 (Seg_D_5, A, not_B, D);
  and and_21 (Seg_D_6, not_A, not_B, C);
  and and_22 (Seg_E_1, not_B, not_D);
  and and_23 (Seg_E_2, C, not_D);
  and and_24 (Seg_E_3, A, B);
  and and_25 (Seg_E_4, A, C);
  and and_26 (Seg_F_1, A, not_B);
  and and_27 (Seg_F_2, C, A);
  and and_28 (Seg_F_3, not_D, C, B);
  and and_29 (Seg_F_4, B, not_A, not_C);
  and and_30 (Seg_F_5, not_A, not_D, not_C);
  and and_31 (Seg_G_1, not_B, C);
  and and_32 (Seg_G_2, B, not_D);
  and and_33 (Seg_G_3, not_C, B);
  or or_1 (Fa, Seg_A_1, Seg_A_2, Seg_A_3, Seg_A_4, Seg_A_5);
  or or_2 (Fb, Seg_B_1, Seg_B_2, Seg_B_3, Seg_B_4, Seg_B_5);
  or or_3 (Fc, Seg_C_1, Seg_C_2, Seg_C_3, Seg_C_4, Seg_C_5);
  or or_4 (Fd, Seg_D_1, Seg_D_2, Seg_D_3, Seg_D_4, Seg_D_5, Seg_D_6);
  or or_5 (Fe, Seg_E_1, Seg_E_2, Seg_E_3, Seg_E_4);
  or or_6 (Ff, Seg_F_1, Seg_F_2, Seg_F_3, Seg_F_4, Seg_F_5);
  or or_7 (Fg, Seg_G_1, Seg_G_2, Seg_G_3, A);
  Seven_Seg seven_seg_1 (.a(Fa), .b(Fb), .c(Fc), .d(Fd), .e(Fe), .f(Ff), .g(Fg), .dp(1'b0));
endmodule
