// Digital circuit register-file.dig as structural Verilog
module register_file (
  input  [4:0] ReadReg1,
  input  [4:0] ReadReg2,
  input  [4:0] WriteReg,
  input  [31:0] WriteData,
  input  RegWrite,
  input  Clock,
  output [31:0] ReadData1,
  output [31:0] ReadData2
);

  wire decoder_1_out_0, decoder_1_out_1, decoder_1_out_2, decoder_1_out_3, decoder_1_out_4, decoder_1_out_5,
       decoder_1_out_6, decoder_1_out_7, decoder_1_out_8, decoder_1_out_9, decoder_1_out_10,
       decoder_1_out_11, decoder_1_out_12, decoder_1_out_13, decoder_1_out_14, decoder_1_out_15,
       decoder_1_out_16, decoder_1_out_17, decoder_1_out_18, decoder_1_out_19, decoder_1_out_20,
       decoder_1_out_21, decoder_1_out_22, decoder_1_out_23, decoder_1_out_24, decoder_1_out_25,
       decoder_1_out_26, decoder_1_out_27, decoder_1_out_28, decoder_1_out_29, decoder_1_out_30,
       decoder_1_out_31, Load_1, Load_2, Load_3, Load_4, Load_5, Load_6, Load_7, Load_8, Load_9, Load_10,
       Load_11, Load_12, Load_13, Load_14, Load_15, Load_16, Load_17, Load_18, Load_19, Load_20, Load_21,
       Load_22, Load_23, Load_24, Load_25, Load_26, Load_27, Load_28, Load_29, Load_30, Load_31, Load_32;
  wire [31:0] Q1, Q2, Q3, Q4, Q5, Q6, Q7, Q8, Q9, Q10, Q11, Q12, Q13, Q14, Q15, Q16, Q17, Q18, Q19, Q20, Q21,
       Q22, Q23, Q24, Q25, Q26, Q27, Q28, Q29, Q30, Q31, Q32;

  Decoder #(.Selector_Bits(5)) decoder_1 (
    .sel(WriteReg), .out_0(decoder_1_out_0), .out_1(decoder_1_out_1), .out_2(decoder_1_out_2),
    .out_3(decoder_1_out_3), .out_4(decoder_1_out_4), .out_5(decoder_1_out_5), .out_6(decoder_1_out_6),
    .out_7(decoder_1_out_7), .out_8(decoder_1_out_8), .out_9(decoder_1_out_9), .out_10(decoder_1_out_10),
    .out_11(decoder_1_out_11), .out_12(decoder_1_out_12), .out_13(decoder_1_out_13),
    .out_14(decoder_1_out_14), .out_15(decoder_1_out_15), .out_16(decoder_1_out_16),
    .out_17(decoder_1_out_17), .out_18(decoder_1_out_18), .out_19(decoder_1_out_19),
    .out_20(decoder_1_out_20), .out_21(decoder_1_out_21), .out_22(decoder_1_out_22),
    .out_23(decoder_1_out_23), .out_24(decoder_1_out_24), .out_25(decoder_1_out_25),
    .out_26(decoder_1_out_26), .out_27(decoder_1_out_27), .out_28(decoder_1_out_28),
    .out_29(decoder_1_out_29), .out_30(decoder_1_out_30), .out_31(decoder_1_out_31));
  and and_1 (Load_1, decoder_1_out_0, 1'b0);
  and and_2 (Load_2, decoder_1_out_1, RegWrite);
  and and_3 (Load_3, decoder_1_out_2, RegWrite);
  and and_4 (Load_4, decoder_1_out_3, RegWrite);
  and and_5 (Load_5, decoder_1_out_4, RegWrite);
  and and_6 (Load_6, decoder_1_out_5, RegWrite);
  and and_7 (Load_7, decoder_1_out_6, RegWrite);
  and and_8 (Load_8, decoder_1_out_7, RegWrite);
  and and_9 (Load_9, decoder_1_out_8, RegWrite);
  and and_10 (Load_10, decoder_1_out_9, RegWrite);
  and and_11 (Load_11, decoder_1_out_10, RegWrite);
  and and_12 (Load_12, decoder_1_out_11, RegWrite);
  and and_13 (Load_13, decoder_1_out_12, RegWrite);
  and and_14 (Load_14, decoder_1_out_13, RegWrite);
  and and_15 (Load_15, decoder_1_out_14, RegWrite);
  and and_16 (Load_16, decoder_1_out_15, RegWrite);
  and and_17 (Load_17, decoder_1_out_16, RegWrite);
  and and_18 (Load_18, decoder_1_out_17, RegWrite);
  and and_19 (Load_19, decoder_1_out_18, RegWrite);
  and and_20 (Load_20, decoder_1_out_19, RegWrite);
  and and_21 (Load_21, decoder_1_out_20, RegWrite);
  and and_22 (Load_22, decoder_1_out_21, RegWrite);
  and and_23 (Load_23, decoder_1_out_22, RegWrite);
  and and_24 (Load_24, decoder_1_out_23, RegWrite);
  and and_25 (Load_25, decoder_1_out_24, RegWrite);
  and and_26 (Load_26, decoder_1_out_25, RegWrite);
  and and_27 (Load_27, decoder_1_out_26, RegWrite);
  and and_28 (Load_28, decoder_1_out_27, RegWrite);
  and and_29 (Load_29, decoder_1_out_28, RegWrite);
  and and_30 (Load_30, decoder_1_out_29, RegWrite);
  and and_31 (Load_31, decoder_1_out_30, RegWrite);
  and and_32 (Load_32, decoder_1_out_31, RegWrite);
  Multiplexer #(.Bits(32), .Selector_Bits(5)) multiplexer_1 (
    .sel(ReadReg1), .in_0(Q1), .in_1(Q2), .in_2(Q3), .in_3(Q4), .in_4(Q5), .in_5(Q6), .in_6(Q7), .in_7(Q8),
    .in_8(Q9), .in_9(Q10), .in_10(Q11), .in_11(Q12), .in_12(Q13), .in_13(Q14), .in_14(Q15), .in_15(Q16),
    .in_16(Q17), .in_17(Q18), .in_18(Q19), .in_19(Q20), .in_20(Q21), .in_21(Q22), .in_22(Q23), .in_23(Q24),
    .in_24(Q25), .in_25(Q26), .in_26(Q27), .in_27(Q28), .in_28(Q29), .in_29(Q30), .in_30(Q31), .in_31(Q32),
    .out(ReadData1));
  Register #(.Bits(32)) R0 (.D(WriteData), .C(Clock), .en(Load_1), .Q(Q1));
  Register #(.Bits(32)) R8 (.D(WriteData), .C(Clock), .en(Load_9), .Q(Q9));
  Register #(.Bits(32)) R16 (.D(WriteData), .C(Clock), .en(Load_17), .Q(Q17));
  Register #(.Bits(32)) R24 (.D(WriteData), .C(Clock), .en(Load_25), .Q(Q25));
  Register #(.Bits(32)) R1 (.D(WriteData), .C(Clock), .en(Load_2), .Q(Q2));
  Register #(.Bits(32)) R9 (.D(WriteData), .C(Clock), .en(Load_10), .Q(Q10));
  Register #(.Bits(32)) R17 (.D(WriteData), .C(Clock), .en(Load_18), .Q(Q18));
  Register #(.Bits(32)) R25 (.D(WriteData), .C(Clock), .en(Load_26), .Q(Q26));
  Multiplexer #(.Selector_Bits(5), .Bits(32)) multiplexer_2 (
    .sel(ReadReg2), .in_0(Q1), .in_1(Q2), .in_2(Q3), .in_3(Q4), .in_4(Q5), .in_5(Q6), .in_6(Q7), .in_7(Q8),
    .in_8(Q9), .in_9(Q10), .in_10(Q11), .in_11(Q12), .in_12(Q13), .in_13(Q14), .in_14(Q15), .in_15(Q16),
    .in_16(Q17), .in_17(Q18), .in_18(Q19), .in_19(Q20), .in_20(Q21), .in_21(Q22), .in_22(Q23), .in_23(Q24),
    .in_24(Q25), .in_25(Q26), .in_26(Q27), .in_27(Q28), .in_28(Q29), .in_29(Q30), .in_30(Q31), .in_31(Q32),
    .out(ReadData2));
  Register #(.Bits(32)) R2 (.D(WriteData), .C(Clock), .en(Load_3), .Q(Q3));
  Register #(.Bits(32)) R10 (.D(WriteData), .C(Clock), .en(Load_11), .Q(Q11));
  Register #(.Bits(32)) R18 (.D(WriteData), .C(Clock), .en(Load_19), .Q(Q19));
  Register #(.Bits(32)) R26 (.D(WriteData), .C(Clock), .en(Load_27), .Q(Q27));
  Register #(.Bits(32)) R3 (.D(WriteData), .C(Clock), .en(Load_4), .Q(Q4));
  Register #(.Bits(32)) R11 (.D(WriteData), .C(Clock), .en(Load_12), .Q(Q12));
  Register #(.Bits(32)) R19 (.D(WriteData), .C(Clock), .en(Load_20), .Q(Q20));
  Register #(.Bits(32)) R27 (.D(WriteData), .C(Clock), .en(Load_28), .Q(Q28));
  Register #(.Bits(32)) R4 (.D(WriteData), .C(Clock), .en(Load_5), .Q(Q5));
  Register #(.Bits(32)) R12 (.D(WriteData), .C(Clock), .en(Load_13), .Q(Q13));
  Register #(.Bits(32)) R20 (.D(WriteData), .C(Clock), .en(Load_21), .Q(Q21));
  Register #(.Bits(32)) R28 (.D(WriteData), .C(Clock), .en(Load_29), .Q(Q29));
  Register #(.Bits(32)) R5 (.D(WriteData), .C(Clock), .en(Load_6), .Q(Q6));
  Register #(.Bits(32)) R13 (.D(WriteData), .C(Clock), .en(Load_14), .Q(Q14));
  Register #(.Bits(32)) R21 (.D(WriteData), .C(Clock), .en(Load_22), .Q(Q22));
  Register #(.Bits(32)) R29 (.D(WriteData), .C(Clock), .en(Load_30), .Q(Q30));
  Register #(.Bits(32)) R6 (.D(WriteData), .C(Clock), .en(Load_7), .Q(Q7));
  Register #(.Bits(32)) R14 (.D(WriteData), .C(Clock), .en(Load_15), .Q(Q15));
  Register #(.Bits(32)) R22 (.D(WriteData), .C(Clock), .en(Load_23), .Q(Q23));
  Register #(.Bits(32)) R30 (.D(WriteData), .C(Clock), .en(Load_31), .Q(Q31));
  Register #(.Bits(32)) R7 (.D(WriteData), .C(Clock), .en(Load_8), .Q(Q8));
  Register #(.Bits(32)) R15 (.D(WriteData), .C(Clock), .en(Load_16), .Q(Q16));
  Register #(.Bits(32)) R23 (.D(WriteData), .C(Clock), .en(Load_24), .Q(Q24));
  Register #(.Bits(32)) R31 (.D(WriteData), .C(Clock), .en(Load_32), .Q(Q32));

  // Other names for the same wires on the sheet: Clk = Clock; RR = RegWrite; WD[31:0] = WriteData
endmodule

/* Test case Register File Test:
WriteReg WriteData RegWrite Clock ReadReg1 ReadReg2 ReadData1 ReadData2

# $1 = 25
1 25 1 C 1 0 25 0

# $2 = 30
2 30 1 C 0 2 0 30

# $(N+1) = (N+1)
loop(N, 30)
	(N+1) (N+1) 1 C (N+1) (N) (N+1) (N)
end loop

# $(N+1) = N-60
loop(N, 30)
	(N+1) (N-60) 1 C (N+1) (N+1) (N-60) (N-60)
end loop

# Try writing to $0. This should not write anything
0 25 1 C 0 0 0 0

# try writing when RegWrite = 0
# (the registers should still have their old values)
loop(N, 30)
	(N+1) (N+80) 0 C (N+1) (N+1) (N-60) (N-60)
end loop
*/
